# Fritzing sketch Sensorstation (saved by Fritzing 0.9.3b)
breadboards: 1

parts:
  Arduino = Arduino Nano 33 BLE Sense
  T1 = LTR-301 [package=ltr-301]
  SW1 = DIP Switch 8 Position [package=dipswitch-08]
  R7 = Bussed8 Resistor-8 (SIP-9) [tolerance=±5% resistance=10k package=SIP-9]
  Piezo_Buzzer = Piezo Speaker
  Adafruit = Adafruit BME680 [part_number=" BME688"]
  R5 = Resistor [tolerance=±5% resistance=10k package=THT]
  R2 = Resistor [tolerance=±5% resistance=220 package=THT]
  R3 = Resistor [tolerance=±5% resistance=220 package=THT]
  R4 = Resistor [tolerance=±5% resistance=220 package=THT]
  S1 = Pushbutton [package=THT]
  R6 = Resistor [tolerance=±5% resistance=10k package=THT]
  S2 = Pushbutton [package=THT]
  R1 = Resistor [tolerance=±5% resistance=2k package=THT]
  KeeYees = Humidity and Temperature Sensor RHT03 [part_number="analogue Hygrometer"]
  LED1 = RGB LED (com. cathode, rbg) [package="5 mm [THT]"]

nets:
  N1: Arduino.TX, R3.Pin_0
  N2: Arduino.RX, R2.Pin_0
  N3: Arduino.D2, R4.Pin_0
  N4: Arduino.D3~, R5.Pin_1, S1.leg1
  N5: Arduino.D4, R6.Pin_1, S2.leg1
  N6: Arduino.D5~, SW1.1, R7.Pin_8
  N7: Arduino.D6~, SW1.2, R7.Pin_7
  N8: Arduino.D7, SW1.3, R7.Pin_6
  N9: Arduino.D8, SW1.4, R7.Pin_5
  N10: Arduino.D9~, SW1.5, R7.Pin_4
  N11: Arduino.D10~, SW1.6, R7.Pin_3
  N12: Arduino.D11/MOSI, SW1.7, R7.Pin_2
  N13: Arduino.D12~/MISO, SW1.8, R7.Pin_1
  GND: Arduino.GND, Arduino.A7, T1.E, SW1.9, SW1.10, SW1.11, SW1.12, SW1.13, SW1.14, SW1.15, SW1.16, Piezo_Buzzer.pin1, Adafruit.GND, S1.leg0, S2.leg0, R1.Pin_0, R1.Pin_1, KeeYees.GND_2, LED1.common_cathode
  N14: Arduino.A6, KeeYees.Data-signal
  N15: Arduino.A5, Adafruit.SCK/SCL
  N16: Arduino.A4, Adafruit.SDI/SDA
  N17: Arduino.A3, Piezo_Buzzer.pin2
  VCC: Arduino.3V3, T1.C, R7.Pin_0, Adafruit.VCC, R5.Pin_0, R6.Pin_0, KeeYees.Vcc
  N18: R2.Pin_1, LED1.red_anode
  N19: R3.Pin_1, LED1.blue_anode
  N20: R4.Pin_1, LED1.green_anode

custom parts:
  Arduino Nano 33 BLE Sense: The Nano 33 BLE Sense (without headers) is Arduino’s 3.3V AI enabled board in the smallest available form factor: 45x18mm! The Arduino Nano 33 BLE Sense is a completely new board on a well-known form factor. It comes with a series of embedded sensors: 9 axis inertial sensor: what makes this board ideal for wearable devices humidity, and temperature sensor: to get highly accurate measurements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
  Bussed8 Resistor-8 (SIP-9): A resistor array is a single package which contains more than one resistor. They are typically used for convenience when several resistors are needed together in the same place in a circuit.
  Humidity and Temperature Sensor RHT03: Digital relative humidity & temperature sensor RHT03
